# Fritzing sketch Full_Design (saved by Fritzing 0.9.3b)
circuit board: 8.46667cm x 5.64444cm
breadboards: 4

parts:
  R2 = Resistor [tolerance=±5% resistance=2.2k package=THT]
  Force_Sensitive_Resistor = Basic Force Sensing Resistor (FSR) [package=THT]
  R3 = Resistor [tolerance=±5% resistance=2.2k package=THT]
  R4 = Resistor [tolerance=±5% resistance=2.2k package=THT]
  R5 = Resistor [tolerance=±5% resistance=2.2k package=THT]
  R6 = Resistor [tolerance=±5% resistance=2.2k package=THT]
  R7 = Resistor [tolerance=±5% resistance=2.2k package=THT]
  R8 = Resistor [tolerance=±5% resistance=2.2k package=THT]
  R11 = Resistor [tolerance=±5% resistance=2.2k package=THT]
  R12 = Resistor [tolerance=±5% resistance=2.2k package=THT]
  R13 = Resistor [tolerance=±5% resistance=2.2k package=THT]
  R14 = Resistor [tolerance=±5% resistance=2.2k package=THT]
  Base_Resistors = Resistor [tolerance=±5% resistance=2.2k package=THT]
  R16 = Resistor [tolerance=±5% resistance=2.2k package=THT]
  R17 = Resistor [tolerance=±5% resistance=2.2k package=THT]
  R19 = Resistor [tolerance=±5% resistance=2.2k package=THT]
  R20 = Resistor [tolerance=±5% resistance=2.2k package=THT]
  R22 = Resistor [tolerance=±5% resistance=2.2k package=THT]
  Piezo_Buzzer = Piezo Speaker
  part = Resistor [tolerance=±5% resistance=1.5M package=THT]
  R9 = Resistor [tolerance=±5% resistance=2.2k package=THT]
  U14 = TRANSISTOR_NPN_2 [package=to-92]
  R36 = Resistor [tolerance=±5% resistance=68 package=THT]
  LED21 = LED - 5mm [color="Red (633nm)" package="5 mm [THT]"]
  LED22 = LED - 5mm [color="Red (633nm)" package="5 mm [THT]"]
  U15 = TRANSISTOR_NPN_2 [package=to-92]
  R37 = Resistor [tolerance=±5% resistance=68 package=THT]
  LED23 = LED - 5mm [color="Red (633nm)" package="5 mm [THT]"]
  LED24 = LED - 5mm [color="Red (633nm)" package="5 mm [THT]"]
  U16 = TRANSISTOR_NPN_2 [package=to-92]
  R38 = Resistor [tolerance=±5% resistance=68 package=THT]
  LED25 = LED - 5mm [color="Red (633nm)" package="5 mm [THT]"]
  LED26 = LED - 5mm [color="Red (633nm)" package="5 mm [THT]"]
  U17 = TRANSISTOR_NPN_2 [package=to-92]
  R39 = Resistor [tolerance=±5% resistance=68 package=THT]
  LED27 = LED - 5mm [color="Red (633nm)" package="5 mm [THT]"]
  LED28 = LED - 5mm [color="Red (633nm)" package="5 mm [THT]"]
  U18 = TRANSISTOR_NPN_2 [package=to-92]
  R40 = Resistor [tolerance=±5% resistance=68 package=THT]
  LED29 = LED - 5mm [color="Red (633nm)" package="5 mm [THT]"]
  LED30 = LED - 5mm [color="Red (633nm)" package="5 mm [THT]"]
  U19 = TRANSISTOR_NPN_2 [package=to-92]
  R41 = Resistor [tolerance=±5% resistance=68 package=THT]
  LED31 = LED - 5mm [color="Red (633nm)" package="5 mm [THT]"]
  LED32 = LED - 5mm [color="Red (633nm)" package="5 mm [THT]"]
  U20 = TRANSISTOR_NPN_2 [package=to-92]
  R42 = Resistor [tolerance=±5% resistance=68 package=THT]
  LED33 = LED - 5mm [color="Red (633nm)" package="5 mm [THT]"]
  LED34 = LED - 5mm [color="Red (633nm)" package="5 mm [THT]"]
  U21 = TRANSISTOR_NPN_2 [package=to-92]
  R43 = Resistor [tolerance=±5% resistance=68 package=THT]
  LED35 = LED - 5mm [color="Red (633nm)" package="5 mm [THT]"]
  LED36 = LED - 5mm [color="Red (633nm)" package="5 mm [THT]"]
  U22 = TRANSISTOR_NPN_2 [package=to-92]
  U23 = TRANSISTOR_NPN_2 [package=to-92]
  U24 = TRANSISTOR_NPN_2 [package=to-92]
  U25 = TRANSISTOR_NPN_2 [package=to-92]
  U26 = TRANSISTOR_NPN_2 [package=to-92]
  U27 = TRANSISTOR_NPN_2 [package=to-92]
  U28 = TRANSISTOR_NPN_2 [package=to-92]
  U29 = TRANSISTOR_NPN_2 [package=to-92]
  LED_Driver_Circuit = TRANSISTOR_NPN_2 [part_number=2N5088 package=to-92]
  U31 = TRANSISTOR_NPN_2 [package=to-92]
  R44 = Resistor [tolerance=±5% resistance=68 package=THT]
  R45 = Resistor [tolerance=±5% resistance=68 package=THT]
  R46 = Resistor [tolerance=±5% resistance=68 package=THT]
  R47 = Resistor [tolerance=±5% resistance=68 package=THT]
  R48 = Resistor [tolerance=±5% resistance=68 package=THT]
  R49 = Resistor [tolerance=±5% resistance=68 package=THT]
  R50 = Resistor [tolerance=±5% resistance=68 package=THT]
  R51 = Resistor [tolerance=±5% resistance=68 package=THT]
  R53 = Resistor [tolerance=±5% resistance=68 package=THT]
  LED37 = LED - 5mm [color="Red (633nm)" package="5 mm [THT]"]
  LED38 = LED - 5mm [color="Red (633nm)" package="5 mm [THT]"]
  LED39 = LED - 5mm [color="Red (633nm)" package="5 mm [THT]"]
  LED_Array = LED - 5mm [color="Red (633nm)" package="5 mm [THT]"]
  LED41 = LED - 5mm [color="Red (633nm)" package="5 mm [THT]"]
  LED42 = LED - 5mm [color="Red (633nm)" package="5 mm [THT]"]
  LED43 = LED - 5mm [color="Red (633nm)" package="5 mm [THT]"]
  LED44 = LED - 5mm [color="Red (633nm)" package="5 mm [THT]"]
  LED45 = LED - 5mm [color="Red (633nm)" package="5 mm [THT]"]
  LED46 = LED - 5mm [color="Red (633nm)" package="5 mm [THT]"]
  LED47 = LED - 5mm [color="Red (633nm)" package="5 mm [THT]"]
  LED48 = LED - 5mm [color="Red (633nm)" package="5 mm [THT]"]
  LED49 = LED - 5mm [color="Red (633nm)" package="5 mm [THT]"]
  LED50 = LED - 5mm [color="Red (633nm)" package="5 mm [THT]"]
  LED51 = LED - 5mm [color="Red (633nm)" package="5 mm [THT]"]
  LED52 = LED - 5mm [color="Red (633nm)" package="5 mm [THT]"]
  LED53 = LED - 5mm [color="Red (633nm)" package="5 mm [THT]"]
  LED54 = LED - 5mm [color="Red (633nm)" package="5 mm [THT]"]
  LED55 = LED - 5mm [color="Red (633nm)" package="5 mm [THT]"]
  LED56 = LED - 5mm [color="Red (633nm)" package="5 mm [THT]"]
  Part1 = Arduino Uno (Rev3)
  Collector_Resistors = Resistor [tolerance=±5% resistance=68 package=THT]
  part_2 = 2.1mm Barrel Jack with Terminal Block [part_number="9V DC Input"]

nets:
  N1: R2.Pin_0, U17.B
  N2: R2.Pin_1, Part1.D13/SCK
  N3: Force_Sensitive_Resistor.pin_0, part.Pin_1
  N4: Force_Sensitive_Resistor.pin_1, Part1.A0
  N5: R3.Pin_0, U15.B
  N6: R3.Pin_1, Part1.D11_PWM/MOSI
  N7: R4.Pin_0, U16.B
  N8: R4.Pin_1, Part1.D12/MISO
  N9: R5.Pin_0, U14.B
  N10: R5.Pin_1, Part1.D10_PWM/SS
  N11: R6.Pin_0, LED_Driver_Circuit.B
  N12: R6.Pin_1, Part1.D9_PWM
  N13: R7.Pin_0, U27.B
  N14: R7.Pin_1, Part1.D8
  N15: R8.Pin_0, U25.B
  N16: R8.Pin_1, Part1.D7
  N17: R11.Pin_0, U26.B
  N18: R11.Pin_1, Part1.D6_PWM
  N19: R12.Pin_0, U23.B
  N20: R12.Pin_1, Part1.D1/TX
  N21: R13.Pin_0, U28.B
  N22: R13.Pin_1, Part1.D4
  N23: R14.Pin_0, U29.B
  N24: R14.Pin_1, Part1.D5_PWM
  N25: Base_Resistors.Pin_0, U31.B
  N26: Base_Resistors.Pin_1, Part1.D2
  N27: R16.Pin_0, U19.B
  N28: R16.Pin_1, Part1.A4/SDA
  N29: R17.Pin_0, U18.B
  N30: R17.Pin_1, Part1.A5/SCL
  N31: R19.Pin_0, U21.B
  N32: R19.Pin_1, Part1.A2
  N33: R20.Pin_0, U22.B
  N34: R20.Pin_1, Part1.A1
  N35: R22.Pin_0, U20.B
  N36: R22.Pin_1, Part1.A3
  N37: Piezo_Buzzer.pin1, part.Pin_0
  N38: Piezo_Buzzer.pin2, Part1.D3_PWM
  N39: R9.Pin_0, U24.B
  N40: R9.Pin_1, Part1.D0/RX
  N41: U14.C, LED22.cathode
  N42: U14.E, U15.E, U16.E, U17.E, U18.E, U19.E, U20.E, U21.E, U22.E, U23.E, U24.E, U25.E, U26.E, U27.E, U28.E, U29.E, LED_Driver_Circuit.E, U31.E, Part1.GND, part_2.NEG
  N43: R36.Pin_0, R37.Pin_0, R38.Pin_0, R39.Pin_0, R40.Pin_0, R41.Pin_0, R42.Pin_0, R43.Pin_0, R44.Pin_0, R45.Pin_0, R46.Pin_0, R47.Pin_0, R48.Pin_0, R49.Pin_0, R50.Pin_0, R51.Pin_0, R53.Pin_0, Part1.VIN, Collector_Resistors.Pin_0, part_2.POS
  N44: R36.Pin_1, LED21.anode
  N45: LED21.cathode, LED22.anode
  N46: U15.C, LED24.cathode
  N47: R37.Pin_1, LED23.anode
  N48: LED23.cathode, LED24.anode
  N49: U16.C, LED26.cathode
  N50: R38.Pin_1, LED25.anode
  N51: LED25.cathode, LED26.anode
  N52: U17.C, LED28.cathode
  N53: R39.Pin_1, LED27.anode
  N54: LED27.cathode, LED28.anode
  N55: U18.C, LED30.cathode
  N56: R40.Pin_1, LED29.anode
  N57: LED29.cathode, LED30.anode
  N58: U19.C, LED32.cathode
  N59: R41.Pin_1, LED31.anode
  N60: LED31.cathode, LED32.anode
  N61: U20.C, LED34.cathode
  N62: R42.Pin_1, LED33.anode
  N63: LED33.cathode, LED34.anode
  N64: U21.C, LED36.cathode
  N65: R43.Pin_1, LED35.anode
  N66: LED35.cathode, LED36.anode
  N67: U22.C, LED46.cathode
  N68: U23.C, LED39.cathode
  N69: U24.C, LED53.cathode
  N70: U25.C, LED50.cathode
  N71: U26.C, LED38.cathode
  N72: U27.C, LED45.cathode
  N73: U28.C, LED47.cathode
  N74: U29.C, LED52.cathode
  N75: LED_Driver_Circuit.C, LED41.cathode
  N76: U31.C, LED56.cathode
  N77: R44.Pin_1, LED51.anode
  N78: R45.Pin_1, LED37.anode
  N79: R46.Pin_1, LED49.anode
  N80: R47.Pin_1, LED48.anode
  N81: R48.Pin_1, LED42.anode
  N82: R49.Pin_1, LED44.anode
  N83: R50.Pin_1, LED55.anode
  N84: R51.Pin_1, LED43.anode
  N85: R53.Pin_1, LED54.anode
  N86: LED37.cathode, LED50.anode
  N87: LED38.anode, LED54.cathode
  N88: LED39.anode, LED55.cathode
  N89: LED_Array.cathode, LED41.anode
  N90: LED_Array.anode, Collector_Resistors.Pin_1
  N91: LED42.cathode, LED53.anode
  N92: LED43.cathode, LED56.anode
  N93: LED44.cathode, LED47.anode
  N94: LED45.anode, LED48.cathode
  N95: LED46.anode, LED51.cathode
  N96: LED49.cathode, LED52.anode
