# Fritzing sketch LED_Driver_Design (saved by Fritzing 0.9.3b)
breadboards: 1

parts:
  RB = Resistor [tolerance=±5% resistance=10k package=THT]
  RC = Resistor [tolerance=±5% resistance=75 package=THT]
  LED21 = LED - 5mm [color="Red (633nm)" package="5 mm [THT]"]
  LED22 = LED - 5mm [color="Red (633nm)" package="5 mm [THT]"]
  Part1 = Arduino Uno (Rev3)
  part = 2.1mm Barrel Jack with Terminal Block [part_number="9V DC Input"]
  2N5088 = NPN-Transistor [package="TO92 [THT]"]

nets:
  N1: RB.Pin_0, 2N5088.B
  N2: RB.Pin_1, Part1.D10_PWM/SS
  N3: RC.Pin_0, Part1.VIN, part.POS
  N4: RC.Pin_1, LED21.anode
  N5: LED21.cathode, LED22.anode
  N6: LED22.cathode, 2N5088.C
  N7: Part1.GND, part.NEG, 2N5088.E
